// Logisim project Week4.1.circ as structural Verilog: 1 circuit, main circuit main
module main (
  input  A,
  input  B,
  input  C,
  output F
);

  wire or_1_out, or_2_out, xor_1_out, xor_2_out;

  xor xor_1 (xor_1_out, A, B);
  xor xor_2 (xor_2_out, B, C);
  or or_1 (or_1_out, xor_1_out, C);
  or or_2 (or_2_out, A, xor_2_out);
  and and_1 (F, or_1_out, or_2_out);
endmodule
