// Logisim project Week4.2.circ as structural Verilog: 1 circuit, main circuit main
module main (
  input  in_1,
  input  in_2,
  input  A,
  input  [1:0] CB,
  output F2,
  output F1
);

  wire not_1_out;

  not not_1 (not_1_out, A);
  Multiplexer #(.select(2), .enable("false")) multiplexer_1 (
    .in0(in_1), .in1(A), .in2(A), .in3(in_2), .out(F2), .sel(CB));
  Multiplexer #(.select(2), .enable("false")) multiplexer_2 (
    .in0(A), .in1(not_1_out), .in2(not_1_out), .in3(A), .out(F1), .sel(CB));
endmodule
