// Logisim project 线下作业.circ as structural Verilog: 1 circuit, main circuit main
module main (
  input  in_1,
  input  in_2
);

  wire and_1_out, and_2_out, and_3_out, clock_1_out, D1_q, D1_qn, D2_q, D2_qn, D3_q, D3_qn, not_1_out;

  not not_1 (not_1_out, in_2);
  Clock clock_1 (.out(clock_1_out));
  and and_1 (and_1_out, not_1_out, D1_qn, D2_q, D3_qn);
  // Probe on D3_q
  D_Flip_Flop D3 (.clk(clock_1_out), .D(and_1_out), .Q(D3_q), .Qn(D3_qn), .en(in_1));  // open: preset, reset
  and and_2 (and_2_out, D3_qn, D1_q);
  // Probe on and_3_out
  and and_3 (and_3_out, in_2, D3_q, D2_qn, D1_qn);
  // Probe on D2_q
  D_Flip_Flop D2 (.clk(clock_1_out), .D(and_2_out), .Q(D2_q), .Qn(D2_qn), .en(in_1));  // open: preset, reset
  // Probe on D1_q
  D_Flip_Flop D1 (.clk(clock_1_out), .D(in_2), .Q(D1_q), .Qn(D1_qn), .en(in_1));  // open: preset, reset
endmodule
